# Fritzing sketch sketch (saved by Fritzing 0.8.3b)

parts:
  Part1 = Arduino Mega 2560 (Rev3)
  U1 = LCD-16X2 [package=lcd-16x2]
  U2 = RJ45 Jack [package=rj45-8]
  R1 = Rotary Potentiometer (Small)
  R2 = Resistor [tolerance=±5% resistance=220 package=THT]
  K1 = Relay [part_number=FRS1B-S package=THT]
  K6 = Relay [part_number=FRS1B-S package=THT]
  K4 = Relay [part_number=FRS1B-S package=THT]
  K7 = Relay [part_number=FRS1B-S package=THT]
  K2 = Relay [part_number=FRS1B-S package=THT]
  K5 = Relay [part_number=FRS1B-S package=THT]
  K8 = Relay [part_number=FRS1B-S package=THT]
  K3 = Relay [part_number=FRS1B-S package=THT]
  JP2 = Header 3 [package=molex-1x3_lock]
  JP3 = Header 3 [package=molex-1x3_lock]
  JP4 = Header 3 [package=molex-1x3_lock]
  JP5 = Header 3 [package=molex-1x3_lock]
  JP6 = Header 3 [package=molex-1x3_lock]
  JP7 = Header 3 [package=molex-1x3_lock]
  JP8 = Header 3 [package=molex-1x3_lock]
  JP9 = Header 3 [package=molex-1x3_lock]

nets:
  N1: Part1.D21/SCL, U2.3
  N2: Part1.D20/SDA, U2.6
  N3: Part1.D10_PWM, U2.1
  N4: Part1.D9_PWM, K1.COIL1
  N5: Part1.D8_PWM, K2.COIL1
  5V: Part1.5V, U1.VDD, U2.7, R2.Pin_0, K1.COIL2, K6.COIL2, K4.COIL2, K7.COIL2, K2.COIL2, K5.COIL2, K8.COIL2, K3.COIL2
  GND: Part1.GND, U1.VSS, U1.R_W, U1.K, U2.8, R1.leg1
  N6: Part1.D2_PWM, K8.COIL1
  N7: Part1.D3_PWM, K7.COIL1
  N8: Part1.D4_PWM, K6.COIL1
  N9: Part1.D5_PWM, K5.COIL1
  N10: Part1.D6_PWM, K4.COIL1
  N11: Part1.D7_PWM, K3.COIL1
  N12: Part1.D22, U1.DB4
  N13: Part1.D23, U1.DB5
  N14: Part1.D24, U1.DB6
  N15: Part1.D25, U1.DB7
  N16: Part1.D26, U1.RS
  N17: Part1.D27, U1.E
  N18: U1.VO, R1.wiper
  N19: U1.A, R2.Pin_1
  N20: K1.A, JP9.1
  N21: K1.C2, JP9.2
  N22: K1.B, JP9.3
  N23: K6.A, JP4.1
  N24: K6.C1, K6.C2, JP4.2
  N25: K6.B, JP4.3
  N26: K4.A, JP6.1
  N27: K4.C2, JP6.2
  N28: K4.B, JP6.3
  N29: K7.A, JP3.1
  N30: K7.C1, K7.C2, JP3.2
  N31: K7.B, JP3.3
  N32: K2.A, JP8.1
  N33: K2.C2, JP8.2
  N34: K2.B, JP8.3
  N35: K5.A, JP5.1
  N36: K5.C1, K5.C2, JP5.2
  N37: K5.B, JP5.3
  N38: K8.A, JP2.1
  N39: K8.C1, K8.C2, JP2.2
  N40: K8.B, JP2.3
  N41: K3.A, JP7.1
  N42: K3.C2, JP7.2
  N43: K3.B, JP7.3

notes:
  To heating heads mounted on heating collector
